# Fritzing sketch flasher (saved by Fritzing 0.9.3b)
breadboards: 1

parts:
  Raspberry_Pi_Zero1 = Raspberry Pi Zero
  LED1 = LED - 3mm [color="Yellow (595nm)" package="3 mm [THT]"]
  LED2 = LED - 3mm [color="Yellow (595nm)" package="3 mm [THT]"]
  LED3 = LED - 3mm [color="Yellow (595nm)" package="3 mm [THT]"]
  LED4 = LED - 3mm [color="Blue (525nm)" package="3 mm [THT]"]
  LED5 = LED - 3mm [color="Red (633nm)" package="3 mm [THT]"]
  LED6 = LED - 3mm [color="Green (570nm)" package="3 mm [THT]"]
  R1 = Resistor [tolerance=±5% resistance=220 package=THT]
  R2 = Resistor [tolerance=±5% resistance=220 package=THT]
  R3 = Resistor [tolerance=±5% resistance=220 package=THT]
  R4 = Resistor [tolerance=±5% resistance=220 package=THT]
  R5 = Resistor [tolerance=±5% resistance=220 package=THT]
  S1 = Round Pushbutton
  S2 = Toggle Switch [package=THT]
  R6 = Resistor [tolerance=±5% resistance=10k package=THT]
  R7 = Resistor [tolerance=±5% resistance=10k package=THT]

nets:
  3V3: Raspberry_Pi_Zero1.3v3, Raspberry_Pi_Zero1.3V3, R6.Pin_0, R7.Pin_0
  N1: Raspberry_Pi_Zero1.GIPO6, LED1.anode
  N2: Raspberry_Pi_Zero1.GIPO13, LED2.anode
  N3: Raspberry_Pi_Zero1.GIPO19, LED3.anode
  N4: Raspberry_Pi_Zero1.GIPO26, LED4.anode
  N5: Raspberry_Pi_Zero1.GND, R1.Pin_1, R2.Pin_1, R3.Pin_1, R4.Pin_1, S1.leg0, S2.L2
  N6: Raspberry_Pi_Zero1.GIPO23, S2.COM, R7.Pin_1
  N7: Raspberry_Pi_Zero1.GIPO18, S1.leg1, R6.Pin_1
  N8: Raspberry_Pi_Zero1.GIPO15, R5.Pin_1
  N9: Raspberry_Pi_Zero1.GIPO14, LED5.anode, LED6.cathode
  N10: LED1.cathode, R1.Pin_0
  N11: LED2.cathode, R2.Pin_0
  N12: LED3.cathode, R3.Pin_0
  N13: LED4.cathode, R4.Pin_0
  N14: LED5.cathode, LED6.anode, R5.Pin_0
